# Fritzing sketch schematicc-electronic (saved by Fritzing 0.9.3b)
breadboards: 2

parts:
  M1 = DOIT Esp32 DevKit v1 (30 pins long, 11 pins width) [part_number=ESP32S-PIN30]
  hc-sr1 = hc-sr04
  Composant1 = HC-SR501 Body Sensor Module
  S1 = H-Bridge with L298N
  S2 = H-Bridge with L298N
  J1 = Basic Servo
  M2 = DC Motor
  M3 = DC Motor
  M4 = DC Motor
  M5 = DC Motor
  Composant2 = LCD1602-I2C
  VCC1 = Battery
  U2 = LM2596 step down module
  R2 = Resistor [tolerance=±5% resistance=220 package="2010 [SMD]"]
  R3 = Resistor [tolerance=±5% resistance=220 package="2010 [SMD]"]

nets:
  N1: M1.D15, S2.IN1
  N2: M1.D2, S2.IN4
  N3: M1.D4, S1.IN4
  N4: M1.D5, S2.IN2
  N5: M1.D18, S2.ENB
  N6: M1.D19, S2.IN3
  N7: M1.D21, Composant2.SDA
  N8: M1.D22, Composant2.SCL
  VCC: hc-sr1.VCC, Composant1.VCC, J1.vcc, Composant2.VCC, U2.OUT+
  N9: hc-sr1.Echo, R2.Pin_1
  GND: hc-sr1.GND, Composant1.GND, S1.GND, S2.GND, J1.gnd, Composant2.GND, VCC1.-, U2.IN-, U2.OUT-, R3.Pin_1
  12V: S1.12V, S2.12V, VCC1.+, U2.IN+
  N10: S1.M1-01, M5.pin_1
  N11: S1.M1-02, M5.pin_2
  N12: S1.M2-01, M4.pin_2
  N13: S1.M2-02, M4.pin_1
  N14: S2.M1-01, M3.pin_1
  N15: S2.M1-02, M3.pin_2
  N16: S2.M2-01, M2.pin_2
  N17: S2.M2-02, M2.pin_1
  N18: R2.Pin_0, R3.Pin_0

custom parts:
  DOIT Esp32 DevKit v1 (30 pins long, 11 pins width): The DOIT Esp32 DevKit v1 is one of the development board created by DOIT to evaluate the ESP-WROOM-32 module. It is based on the ESP32 microcontroller that boasts Wifi, Bluetooth, Ethernet and Low Power support all in a single chip. (vanepp) made breadboard work, adjusted pin numbering and labels and reduced size of schematic and cleaned up pcb. This chip is 30pins long (2 x15) and 11 pins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
  HC-SR501 Body Sensor Module: Pyroelectric Infrared PIR Motion Sensor Detector Module
  H-Bridge with L298N: h-bridge
  LCD1602-I2C: A standard character display, usually with 2x16 characters. Comes in many colors with LCM1602 IIC attached.
  LM2596 step down module: LM2596 DC-DC step down power supply module 3 A.
